# Fritzing sketch thermostatPower (saved by Fritzing 0.9.3b)
breadboards: 1

parts:
  VCC1 = Battery block 9V
  U8 = Voltage Regulator - 3.3V [part_number=LM1086IT package="TO220 [THT]"]
  U9 = Voltage Regulator - 5V [part_number=L7805CV package="TO220 [THT]"]
  C12 = Tantalum Capacitor [capacitance="1 μF" package="B 3528 [SMD, tantalum]"]
  C15 = Ceramic Capacitor [capacitance=330nF voltage=50V package="0805 [SMD, multilayer]"]
  C16 = Ceramic Capacitor [capacitance=100nF voltage=50V package="100 mil [THT, multilayer]"]
  D2 = Diode [package=diode-1n4001]
  U10 = RELAY [package=relay-t9a-2]
  C17 = Tantalum Capacitor [capacitance="1 μF" package="B 3528 [SMD, tantalum]"]
  R7 = Resistor [tolerance=±5% resistance=1k package=THT]
  R8 = Resistor [tolerance=±5% resistance=1k package=THT]
  LED2 = LED - 5mm [color="Yellow (595nm)" package="5 mm [THT]"]
  LED3 = LED - 5mm [color="Yellow (595nm)" package="5 mm [THT]"]
  Q5 = NPN-Transistor [package="SOT-23 [SMD]"]
  R9 = Resistor [tolerance=±5% resistance=1k package=THT]
  D5 = Diode [package=diode-1n4001]  # not connected
  D6 = Diode [package=diode-1n4001]
  S2 = Toggle Switch [package=THT]

nets:
  N1: VCC1.-, U9.GND, C12.+, C15.0, C16.1, U10.COIL2, C17.-, R8.Pin_0, LED3.cathode, Q5.1
  N2: VCC1.+, D2.A, D6.A
  N3: U8.Output, C17.+, R7.Pin_0
  N4: U8.input_voltage, C12.-, S2.COM
  N5: U9.input_voltage, C15.1
  N6: U9.output_voltage, C16.0, LED2.anode
  N7: U10.MAIN, S2.L2
  N8: U10.NC, S2.L1
  N9: R7.Pin_1, LED3.anode
  N10: R8.Pin_1, LED2.cathode
  N11: Q5.0, R9.Pin_0

notes:
  Regulated +3.3V > to ESP8266 VIN
  Regulated+5V > to 5v PCB
  not regulated 9v > to Arduino VIN
  > to Arduino GPIO
  The switch is used to deliver 3.3v before GPIO connection

custom parts:
  Voltage Regulator - 3.3V: 3.3V DC Voltage Regulator
